// Digital circuit extended-control-unit.dig as structural Verilog
module extended_control_unit (
  input  [15:0] INST,
  input  [15:0] FLAG,
  output [1:0] ALUOP,
  output [2:0] RS1,
  output [2:0] RS2,
  output [2:0] WS,
  output STR,
  output WE,
  output [1:0] DMUX,
  output LDR,
  output FLAGEN
);

  wire and_1_out, and_2_out, and_3_out, and_4_out, demultiplexer_1_out_2, demultiplexer_1_out_3, nor_1_out,
       not_1_out, not_2_out, not_3_out, not_4_out, not_5_out, not_6_out, not_11_out;
  wire [0:0] not_10_out;
  wire [1:0] not_8_out;
  wire [1:1] not_7_out;

  not not_1 (not_1_out, FLAG[0]);
  and and_1 (and_1_out, INST[11], not_1_out);
  not not_2 (not_2_out, INST[12]);
  Multiplexer multiplexer_1 (.sel(and_1_out), .in_0(not_11_out), .in_1(1'b0), .out(WE));
  not not_3 (not_3_out, INST[13]);
  not not_4 (not_4_out, INST[14]);
  not not_5 (not_5_out, INST[15]);
  not not_6 (not_6_out, and_1_out);
  and and_2 (and_2_out, not_5_out, not_4_out, not_3_out, INST[12]);
  and and_3 (and_3_out, not_5_out, INST[14], not_3_out, not_2_out);
  and and_4 (and_4_out, not_5_out, INST[14], not_3_out, not_2_out);
  not not_7 (not_7_out[1], 1'b0);
  not not_8 (not_8_out[0], 1'b0);
  not not_9 (not_8_out[1], 1'b0);
  not not_10 (not_10_out[0], 1'b0);
  Multiplexer #(.Bits(3)) multiplexer_2 (.sel(and_3_out), .in_0(INST[10:8]), .in_1(INST[6:4]), .out(WS));
  not not_11 (not_11_out, and_4_out);
  Multiplexer #(.Bits(3)) multiplexer_3 (.sel(INST[14]), .in_0(INST[2:0]), .in_1(INST[10:8]), .out(RS2));
  Multiplexer #(.Selector_Bits(3), .Bits(2)) multiplexer_4 (
    .sel({INST[15:14], INST[12]}), .in_0({not_7_out[1], 1'b0}), .in_1(not_8_out),
    .in_2({1'b0, not_10_out[0]}), .in_3({1'b0, not_10_out[0]}), .in_4(2'b00), .in_5(2'b00), .in_6(2'b00),
    .in_7(2'b00), .out(DMUX));
  Multiplexer #(.Bits(3)) multiplexer_5 (.sel(and_2_out), .in_0(INST[6:4]), .in_1(INST[10:8]), .out(RS1));
  nor nor_1 (nor_1_out, DMUX[0], DMUX[1]);
  and and_5 (FLAGEN, nor_1_out, not_6_out);
  Demultiplexer #(.Selector_Bits(2)) demultiplexer_1 (
    .sel({INST[14], INST[12]}), .in(1'b1), .out_2(demultiplexer_1_out_2), .out_3(demultiplexer_1_out_3));  // open: out_0, out_1
  and and_6 (STR, demultiplexer_1_out_2, not_6_out);
  and and_7 (LDR, demultiplexer_1_out_3, not_6_out);

  assign ALUOP = INST[13:12];

  // Notes on the sheet:
  //   Z
  //   Rd
  //   Ra
  //   Rb
  //   opcode
endmodule

/* Test case All Tests:
	INST                                    WE  ALUOP  RS1   RS2  WS  STR  LDR DMUX

let aluop  = 0b1000;
let ldrop  = 0b0101;
let strop  = 0b0100;
let movlop = 0b0000;

loop(rd, 1<<3)
loop(ra, 1<<3)
loop(rb, 1<<3)

loop(i, 4)
	((aluop+i)<<12 | rd<<8 | ra<<4 | rb<<0) 1  (i)     (ra)  (rb) (rd)  0   X    0  #test add/sub/and/orr
end loop

	(ldrop    <<12 | rd<<8 | ra<<4 )        1  X       (ra)  x    (rd)  0   1    1  #test ldr
	(strop    <<12 | rd<<8 | ra<<4 )        0  X       (ra)  (rd)  X    1   X    X  #test str
	
	let imm = random(256);
	(movlop   <<12 | rd<<8 | imm )          1  X       X      X   (rd)  0   X    2  #test movl

end loop
end loop
end loop
*/

/* Test case WS:
	INST                                    WS 

let aluop  = 0b1000;
let ldrop  = 0b0101;
let strop  = 0b0100;
let movlop = 0b0000;

loop(rd, 1<<3)
loop(ra, 1<<3)
loop(rb, 1<<3)

loop(i, 4)
	((aluop+i)<<12 | rd<<8 | ra<<4 | rb<<0) (rd)  #test add/sub/and/orr
end loop

	(ldrop    <<12 | rd<<8 | ra<<4 )        (rd)   #test ldr
	(strop    <<12 | rd<<8 | ra<<4 )        X     #test str
	
	let imm = random(256);
	(movlop   <<12 | rd<<8 | imm )          (rd)  #test movl

end loop
end loop
end loop
*/

/* Test case RS1:
	INST                                    RS1  

let aluop  = 0b1000;
let ldrop  = 0b0101;
let strop  = 0b0100;
let movlop = 0b0000;

loop(rd, 1<<3)
loop(ra, 1<<3)
loop(rb, 1<<3)

loop(i, 4)
	((aluop+i)<<12 | rd<<8 | ra<<4 | rb<<0) (ra)  #test add/sub/and/orr
end loop

	(ldrop    <<12 | rd<<8 | ra<<4 )        (ra)  #test ldr
	(strop    <<12 | rd<<8 | ra<<4 )        (ra)  #test str

end loop
end loop
end loop
*/

/* Test case RS2:
	INST                                    RS2  

let aluop  = 0b1000;
let ldrop  = 0b0101;
let strop  = 0b0100;
let movlop = 0b0000;

loop(rd, 1<<3)
loop(ra, 1<<3)
loop(rb, 1<<3)

loop(i, 4)
	((aluop+i)<<12 | rd<<8 | ra<<4 | rb<<0) (rb) #test add/sub/and/orr
end loop
	(strop    <<12 | rd<<8 | ra<<4 )        (rd) #test str

end loop
end loop
end loop
*/

/* Test case STR:
	INST                                    STR 

let aluop  = 0b1000;
let ldrop  = 0b0101;
let strop  = 0b0100;
let movlop = 0b0000;

loop(rd, 1<<3)
loop(ra, 1<<3)
loop(rb, 1<<3)

loop(i, 4)
	((aluop+i)<<12 | rd<<8 | ra<<4 | rb<<0) 0  #test add/sub/and/orr
end loop

	(ldrop    <<12 | rd<<8 | ra<<4 )        0  #test ldr
	(strop    <<12 | rd<<8 | ra<<4 )        1  #test str
	
	let imm = random(256);
	(movlop   <<12 | rd<<8 | imm )          0  #test movl

end loop
end loop
end loop
*/

/* Test case WE:
	INST                                    WE  

let aluop  = 0b1000;
let ldrop  = 0b0101;
let strop  = 0b0100;
let movlop = 0b0000;

loop(rd, 1<<3)
loop(ra, 1<<3)
loop(rb, 1<<3)

loop(i, 4)
	((aluop+i)<<12 | rd<<8 | ra<<4 | rb<<0) 1  #test add/sub/and/orr
end loop

	(ldrop    <<12 | rd<<8 | ra<<4 )        1  #test ldr
	(strop    <<12 | rd<<8 | ra<<4 )        0  #test str
	
	let imm = random(256);
	(movlop   <<12 | rd<<8 | imm )          1  #test movl

end loop
end loop
end loop
*/

/* Test case LDR:
	INST                                    LDR 

let aluop  = 0b1000;
let ldrop  = 0b0101;
let strop  = 0b0100;
let movlop = 0b0000;

loop(rd, 1<<3)
loop(ra, 1<<3)
loop(rb, 1<<3)

loop(i, 4)
	((aluop+i)<<12 | rd<<8 | ra<<4 | rb<<0) X    #test add/sub/and/orr
end loop

	(ldrop    <<12 | rd<<8 | ra<<4 )        1    #test ldr
	(strop    <<12 | rd<<8 | ra<<4 )        X    #test str
	
	let imm = random(256);
	(movlop   <<12 | rd<<8 | imm )          X    #test movl

end loop
end loop
end loop
*/

/* Test case DMUX:
	INST                                    DMUX

let aluop  = 0b1000;
let ldrop  = 0b0101;
let strop  = 0b0100;
let movlop = 0b0000;

loop(rd, 1<<3)
loop(ra, 1<<3)
loop(rb, 1<<3)

loop(i, 4)
	((aluop+i)<<12 | rd<<8 | ra<<4 | rb<<0) 0  #test add/sub/and/orr
end loop

	(ldrop    <<12 | rd<<8 | ra<<4 )        1  #test ldr
	
	let imm = random(256);
	(movlop   <<12 | rd<<8 | imm )          2  #test movl

end loop
end loop
end loop
*/

/* Test case ALUOP:
	INST                                    ALUOP 

let aluop  = 0b1000;
let ldrop  = 0b0101;
let strop  = 0b0100;
let movlop = 0b0000;

loop(rd, 1<<3)
loop(ra, 1<<3)
loop(rb, 1<<3)

loop(i, 4)
	((aluop+i)<<12 | rd<<8 | ra<<4 | rb<<0) (i)    #test add/sub/and/orr
end loop

end loop
end loop
end loop
*/
